# Fritzing sketch Reference_Unit (saved by Fritzing 0.8.7b)
circuit board: 13.3111cm x 9.82162cm

parts:
  FTDI = USB connector [package=THT]
  R1 = Resistor [tolerance=±5% resistance=2k package=THT]
  Q1 = PNP-Transistor [part_number=2N2907 package="TO92 [THT]"]
  Q2 = NPN-Transistor [part_number=2N2222 package="TO92 [THT]"]
  R2 = Resistor [tolerance=±5% resistance=2k package=THT]
  R3 = Resistor [tolerance=±5% resistance=500 package=THT]
  R4 = Resistor [tolerance=±5% resistance=2k package=THT]
  R5 = Resistor [tolerance=±5% resistance=2k package=THT]
  Q3 = PNP-Transistor [part_number=2N2907 package="TO92 [THT]"]
  Q4 = NPN-Transistor [part_number=2N2222 package="TO92 [THT]"]
  R6 = Resistor [tolerance=±5% resistance=500 package=THT]
  R7 = Resistor [tolerance=±5% resistance=2k package=THT]
  R8 = Resistor [tolerance=±5% resistance=2k package=THT]
  Q5 = PNP-Transistor [part_number=2N2907 package="TO92 [THT]"]
  Q6 = NPN-Transistor [part_number=2N2222 package="TO92 [THT]"]
  R9 = Resistor [tolerance=±5% resistance=500 package=THT]
  J1 = female pin header, 4 pins [form="♀ (female)"]
  ATMEGA328P = IC, DIP package, 28 pins [chip_label=ATMEGA328]
  C1 = Ceramic Capacitor [capacitance=22pF package="100 mil [THT, multilayer]"]
  C2 = Ceramic Capacitor [capacitance=22pF package="100 mil [THT, multilayer]"]
  XTAL1 = Crystal [frequency="16 Mhz" package=THT]
  R10 = Resistor [tolerance=±5% resistance=10k package=THT]
  C3 = Electrolytic Capacitor [capacitance=1µF package="100 mil [THT, electrolytic]"]
  C4 = Electrolytic Capacitor [capacitance=1µF package="100 mil [THT, electrolytic]"]
  U1 = Voltage Regulator - 5V [package="TO220 [THT]"]
  C5 = Electrolytic Capacitor [capacitance=1µF package="100 mil [THT, electrolytic]"]
  C6 = Electrolytic Capacitor [capacitance=1µF package="100 mil [THT, electrolytic]"]
  C7 = Electrolytic Capacitor [capacitance=1µF package="100 mil [THT, electrolytic]"]
  J2 = Power Jack [package=power_jack_pth_lock]
  S1 = Pushbutton [package="[THT]"]

nets:
  5V: FTDI.5V, ATMEGA328P.pin1, ATMEGA328P.pin20, R10.Pin_1, C3.+, U1.output_voltage, C6.+
  N1: FTDI.d-, ATMEGA328P.pin2
  N2: FTDI.d+, ATMEGA328P.pin3
  GND: FTDI.chassis6, Q2.E, Q4.E, Q6.E, J1.pin4, ATMEGA328P.pin8, ATMEGA328P.pin22, C1.0, C2.0, U1.GND, C5.-, C6.-, J2.GND, J2.GNDBREAK, S1.Pin_3, S1.Pin_4
  N3: R1.Pin_0, ATMEGA328P.pin17
  N4: R1.Pin_1, Q2.B
  N5: Q1.E, R3.Pin_1, Q3.E, R6.Pin_1, Q5.E, R9.Pin_1, C4.-
  N6: Q1.B, R2.Pin_1
  N7: Q1.C, J1.pin1
  N8: Q2.C, R2.Pin_0, R3.Pin_0
  N9: R4.Pin_0, ATMEGA328P.pin16
  N10: R4.Pin_1, Q4.B
  N11: R5.Pin_0, Q4.C, R6.Pin_0
  N12: R5.Pin_1, Q3.B
  N13: Q3.C, J1.pin2
  N14: R7.Pin_0, ATMEGA328P.pin15
  N15: R7.Pin_1, Q6.B
  N16: R8.Pin_0, Q6.C, R9.Pin_0
  N17: R8.Pin_1, Q5.B
  N18: Q5.C, J1.pin3
  N19: ATMEGA328P.pin7, C3.-
  N20: ATMEGA328P.pin9, C1.1, XTAL1.pin_0
  N21: ATMEGA328P.pin10, C2.1, XTAL1.pin_1
  N22: ATMEGA328P.pin23, ATMEGA328P.pin24, ATMEGA328P.pin25, ATMEGA328P.pin26
  N23: R10.Pin_0, S1.Pin_1, S1.Pin_2
  12V: C4.+, C7.+, J2.PWR
  N24: U1.input_voltage, C5.+, C7.-

notes:
  Common-Ground RGB LED Driver
  Clock
  USB-TTL Adapter
  Standard DC Barrel Connector
  Reset Button
  ToDo:
  - Add software reset
  - Test filter capacitors
  - Deal with unused I/O pins
  Stretch Goals:
  - Multiple LED drivers
  - Utility LCD
  - I2C Daisy-Chain of units.
  Problems:
  - Limited PWM lines
